// Logisim project day1_logic.circ as structural Verilog: 9 circuits, main circuit main
module main (
  input  a0,
  input  b0,
  input  cin,
  input  a1,
  input  b1,
  input  a2,
  input  b2,
  input  a3,
  input  b3,
  output out_10
);

  wire [3:0] fourbitadder_1_s0;

  FourBitAdder fourbitadder_1 (
    .a0(a0), .b0(b0), .cin(cin), .a1(a1), .b1(b1), .a2(a2), .b2(b2), .a3(a3), .b3(b3),
    .s0(fourbitadder_1_s0[0]), .s1(fourbitadder_1_s0[1]), .s2(fourbitadder_1_s0[2]),
    .s3(fourbitadder_1_s0[3]), .cout(out_10));
  Hex_Digit_Display hex_digit_display_1 (.value(fourbitadder_1_s0));  // open: dp
endmodule

module OneBitAdder (
  input  a,
  input  b,
  input  c,
  output s,
  output cout
);

  wire AB_out, AC_out, BC_out;

  and AB (AB_out, b, a);
  and BC (BC_out, c, b);
  and AC (AC_out, c, a);
  xor xor_1 (s, c, b, a);
  or or_1 (cout, AB_out, BC_out, AC_out);
endmodule

module FourBitAdder (
  input  a0,
  input  b0,
  input  cin,
  input  a1,
  input  b1,
  input  a2,
  input  b2,
  input  a3,
  input  b3,
  output s0,
  output s1,
  output s2,
  output s3,
  output cout
);

  wire onebitadder_1_cout, onebitadder_2_cout, onebitadder_3_cout;

  OneBitAdder onebitadder_1 (.a(a0), .b(b0), .c(cin), .s(s0), .cout(onebitadder_1_cout));
  OneBitAdder onebitadder_2 (.a(a1), .b(b1), .c(onebitadder_1_cout), .s(s1), .cout(onebitadder_2_cout));
  OneBitAdder onebitadder_3 (.a(a2), .b(b2), .c(onebitadder_2_cout), .s(s2), .cout(onebitadder_3_cout));
  OneBitAdder onebitadder_4 (.a(a3), .b(b3), .c(onebitadder_3_cout), .s(s3), .cout(cout));
endmodule

module OneBitAddSub (
  input  binv,
  input  a,
  input  b,
  input  cin,
  output s,
  output cout
);

  wire multiplexer_1_out, not_1_out;

  not not_1 (not_1_out, b);
  Multiplexer multiplexer_1 (.in0(b), .in1(not_1_out), .out(multiplexer_1_out), .sel(binv));
  OneBitAdder onebitadder_1 (.a(a), .b(multiplexer_1_out), .c(cin), .s(s), .cout(cout));
endmodule

module FourBitAddSub (
  input  sub,
  input  a0,
  input  b0,
  input  a1,
  input  b1,
  input  a2,
  input  b2,
  input  a3,
  input  b3,
  output out_10
);

  wire onebitaddsub_1_cout, onebitaddsub_2_cout, onebitaddsub_3_cout;
  wire [3:0] onebitaddsub_1_s;

  OneBitAddSub onebitaddsub_1 (
    .binv(sub), .a(a0), .b(b0), .cin(sub), .s(onebitaddsub_1_s[0]), .cout(onebitaddsub_1_cout));
  OneBitAddSub onebitaddsub_2 (
    .binv(sub), .a(a1), .b(b1), .cin(onebitaddsub_1_cout), .s(onebitaddsub_1_s[1]), .cout(onebitaddsub_2_cout));
  OneBitAddSub onebitaddsub_3 (
    .binv(sub), .a(a2), .b(b2), .cin(onebitaddsub_2_cout), .s(onebitaddsub_1_s[2]), .cout(onebitaddsub_3_cout));
  OneBitAddSub onebitaddsub_4 (
    .binv(sub), .a(a3), .b(b3), .cin(onebitaddsub_3_cout), .s(onebitaddsub_1_s[3]), .cout(out_10));
  Hex_Digit_Display hex_digit_display_1 (.value(onebitaddsub_1_s));  // open: dp
endmodule

module RS_latch (
  input  S,
  input  R,
  output Q,
  output Qnot
);

  nand nand_1 (Q, S, Qnot);
  nand nand_2 (Qnot, Q, R);

  // Notes on the sheet:
  //   Cross coupled nand gates
endmodule

module D_latch (
  input  D,
  input  WE,
  output out_3
);

  wire nand_1_out, nand_2_out;

  nand nand_1 (nand_1_out, D, WE);
  nand nand_2 (nand_2_out, WE, ~D);  // NAND_Gate
  RS_latch rs_latch_1 (.S(nand_1_out), .R(nand_2_out), .Q(out_3));  // open: Qnot

  // Notes on the sheet:
  //   D high-level triggered latch
  //   WE = 0 Q is unchanged or constant
endmodule

module EightBitALU (
  input  [7:0] A,
  input  [7:0] B,
  input  [1:0] opcode,
  output [7:0] out_4,
  output Z
);

  wire [7:0] adder_1_out, and_1_out, not_1_out, or_1_out, xor_1_out;

  assign or_1_out = A | B;  // OR_Gate or_1, 8 bits wide
  Adder adder_1 (.a(A), .b(B), .out(adder_1_out));  // open: cin, cout
  assign and_1_out = A & B;  // AND_Gate and_1, 8 bits wide
  assign xor_1_out = A ^ B;  // XOR_Gate xor_1, 8 bits wide
  assign not_1_out = ~xor_1_out;  // NOT_Gate not_1, 8 bits wide
  Multiplexer #(.select(2), .width(8)) multiplexer_1 (
    .in0(or_1_out), .in1(adder_1_out), .in2(and_1_out), .in3(not_1_out), .out(out_4), .sel(opcode));
  nor nor_1 (Z, out_4[7], out_4[6], out_4[5], out_4[4], out_4[3], out_4[2], out_4[1], out_4[0]);
endmodule

module RegFile (
  input  [1:0] SR0,
  input  [1:0] SW,
  input  in_3,
  input  [1:0] SR1,
  output [7:0] DataOut0,
  output [7:0] DataOut1
);

  wire demultiplexer_1_out0, demultiplexer_1_out1, demultiplexer_1_out2, demultiplexer_1_out3;
  wire [7:0] register_1_q, register_2_q, register_3_q, register_4_q;

  Demultiplexer #(.select(2)) demultiplexer_1 (
    .out0(demultiplexer_1_out0), .out1(demultiplexer_1_out1), .out2(demultiplexer_1_out2),
    .out3(demultiplexer_1_out3), .in(in_3), .sel(SW));
  Register register_1 (.en(demultiplexer_1_out0), .Q(register_1_q));  // open: D, clk, clr
  Register register_2 (.en(demultiplexer_1_out1), .Q(register_2_q));  // open: D, clk, clr
  Register register_3 (.en(demultiplexer_1_out2), .Q(register_3_q));  // open: D, clk, clr
  Register register_4 (.en(demultiplexer_1_out3), .Q(register_4_q));  // open: D, clk, clr
  Multiplexer #(.select(2), .width(8)) multiplexer_1 (
    .in0(register_1_q), .in1(register_2_q), .in2(register_3_q), .in3(register_4_q), .out(DataOut0), .sel(SR0));
  Multiplexer #(.select(2), .width(8)) multiplexer_2 (
    .in0(register_1_q), .in1(register_2_q), .in2(register_3_q), .in3(register_4_q), .out(DataOut1), .sel(SR1));
endmodule
